# Fritzing sketch useless_box_fritzing (saved by Fritzing 0.9.3b)
breadboards: 1

parts:
  Part1 = Arduino Uno (Rev3) - ICSP  # not connected
  R3 = Resistor [tolerance=±5% resistance=10k package="1206 [SMD]"]
  Part2 = Prototyping Shield
  J1 = Basic Servo  # not connected
  R4 = Resistor [tolerance=±5% resistance=10k package="2010 [SMD]"]
  U1 = SWITCH_SPDT [package=kps-1290]
  U2 = SWITCH_SPDT [package=kps-1290]

nets:
  N1: R3.Pin_0, Part2.D8, U2.O
  N2: R3.Pin_1, Part2.GND#98
  N3: Part2.D9_PWM, R4.Pin_0, U1.O
  N4: Part2.5V#92, U1.P
  N5: Part2.5V#93, U2.P
  N6: Part2.GND#97, R4.Pin_1

custom parts:
  Prototyping Shield: The Arduino Uno is a microcontroller board based on the ATmega328 (datasheet). It has 14 digital input/output pins (of which 6 can be used as PWM outputs), 6 analog inputs, a 16 MHz ceramic resonator, a USB connection, a power jack, an ICSP header, and a reset button. It contains everything needed to support the microcontroller; simply connect it to a computer with a USB cable or power it with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
